# Fritzing sketch sketch (saved by Fritzing 0.9.3b)
breadboards: 2

parts:
  Composant1 = Arduino Nano (Rev3.0)
  LED1 = LED - 5mm [color="Green (570nm)" package="5 mm [THT]"]
  LED2 = LED - 5mm [color="Green (570nm)" package="5 mm [THT]"]
  LED3 = LED - 5mm [color="Green (570nm)" package="5 mm [THT]"]
  LED4 = LED - 5mm [color="Yellow (592nm)" package="5 mm [THT]"]
  LED5 = LED - 5mm [color="Yellow (595nm)" package="5 mm [THT]"]
  LED6 = LED - 5mm [color="Yellow (595nm)" package="5 mm [THT]"]
  LED7 = LED - 5mm [color="Red (633nm)" package="5 mm [THT]"]
  LED8 = LED - 5mm [color="Red (633nm)" package="5 mm [THT]"]
  LED9 = LED - 5mm [color="Red (633nm)" package="5 mm [THT]"]
  LED10 = LED - 5mm [color="Green (570nm)" package="5 mm [THT]"]
  LED11 = LED - 5mm [color="Yellow (592nm)" package="5 mm [THT]"]
  LED12 = LED - 5mm [color="Green (570nm)" package="5 mm [THT]"]
  LED13 = LED - 5mm [color="Green (570nm)" package="5 mm [THT]"]
  LED14 = LED - 5mm [color="Yellow (595nm)" package="5 mm [THT]"]
  LED15 = LED - 5mm [color="Yellow (595nm)" package="5 mm [THT]"]
  LED16 = LED - 5mm [color="Red (633nm)" package="5 mm [THT]"]
  LED17 = LED - 5mm [color="Red (633nm)" package="5 mm [THT]"]
  LED18 = LED - 5mm [color="Red (633nm)" package="5 mm [THT]"]

nets:
  N1: Composant1.GND, LED1.cathode, LED2.cathode, LED3.cathode, LED4.cathode, LED5.cathode, LED6.cathode, LED7.cathode, LED8.cathode, LED9.cathode, LED10.cathode, LED11.cathode, LED12.cathode, LED13.cathode, LED14.cathode, LED15.cathode, LED16.cathode, LED17.cathode, LED18.cathode
  N2: Composant1.D2, LED7.anode
  N3: Composant1.D3, LED8.anode
  N4: Composant1.D4, LED9.anode
  N5: Composant1.D5, LED1.anode
  N6: Composant1.D6, LED2.anode
  N7: Composant1.D7, LED3.anode
  N8: Composant1.D8, LED4.anode
  N9: Composant1.D9, LED5.anode
  N10: Composant1.D10, LED6.anode
  N11: Composant1.D12/MISO, LED10.anode
  N12: Composant1.A7, LED18.anode
  N13: Composant1.A6, LED17.anode
  N14: Composant1.A5, LED16.anode
  N15: Composant1.A4, LED15.anode
  N16: Composant1.A3, LED14.anode
  N17: Composant1.A2, LED11.anode
  N18: Composant1.A1, LED13.anode
  N19: Composant1.A0, LED12.anode

notes:
  CPU
  GPU
